# Fritzing sketch base_wiring (saved by Fritzing 0.9.3b)
breadboards: 1

parts:
  Part1 = Arduino Uno (Rev3)
  R1 = PHOTOCELL [package=photocell-kit]
  LED1 = LED - 5mm [color="Red (633nm)" package="5 mm [THT]"]
  S1 = Pushbutton [package="[THT]"]

nets:
  N1: Part1.A3, R1.P$2
  N2: Part1.D2, LED1.cathode
  N3: R1.P$1, S1.Pin_1, S1.Pin_2
  N4: LED1.anode, S1.Pin_3, S1.Pin_4

notes:
  NOT AN ACTUAL DIAGRAM! JUST TESTING!
